// Logisim project Circuito.circ as structural Verilog: 3 circuits, main circuit Moedeiro
module main (
  input  M1,
  input  M2
);

  wire modulo_servir_cafe_1_lp, moedeiro_1_a, moedeiro_1_b, moedeiro_1_c, moedeiro_1_d, moedeiro_1_e,
       moedeiro_1_f, moedeiro_1_g, moedeiro_1_l;

  Moedeiro moedeiro_1 (
    .M1(M1), .M2(M2), .a(moedeiro_1_a), .b(moedeiro_1_b), .c(moedeiro_1_c), .d(moedeiro_1_d),
    .e(moedeiro_1_e), .f(moedeiro_1_f), .g(moedeiro_1_g), .L(moedeiro_1_l));
  LED led_1 (.in(moedeiro_1_l));
  _7_Segment_Display u_7_segment_display_1 (
    .g(moedeiro_1_g), .f(moedeiro_1_f), .a(moedeiro_1_a), .b(moedeiro_1_b), .e(moedeiro_1_e),
    .d(moedeiro_1_d), .c(moedeiro_1_c));  // open: dp
  LED led_2 (.in(modulo_servir_cafe_1_lp));
  Modulo_servir_cafe modulo_servir_cafe_1 (.B(moedeiro_1_l), .LP(modulo_servir_cafe_1_lp));
endmodule

module Moedeiro (
  input  M1,
  input  M2,
  output a,
  output b,
  output c,
  output d,
  output e,
  output f,
  output g,
  output L
);

  wire and_1_out, and_2_out, and_3_out, and_4_out, and_5_out, and_6_out, and_7_out, and_8_out, and_9_out,
       and_10_out, and_11_out, and_12_out, and_13_out, and_14_out, and_15_out, and_16_out, and_17_out,
       and_18_out, clock_1_out, D0_q, D0_qn, D1_q, D1_qn, not_1_out, not_2_out, or_2_out, or_3_out;

  Clock clock_1 (.out(clock_1_out));
  not not_1 (not_1_out, M2);
  not not_2 (not_2_out, M1);
  and and_1 (and_1_out, M1, M2);
  and and_2 (and_2_out, D0_qn, D1_qn);
  and and_3 (and_3_out, M2, D1_qn);
  and and_4 (and_4_out, D0_q, M1, D1_qn);
  and and_5 (and_5_out, D1_q, D0_qn);
  or or_1 (a, and_1_out, D1_q, and_2_out);
  or or_2 (or_2_out, and_3_out, and_4_out, and_5_out);
  and and_6 (and_6_out, M1, M2, D0_qn);
  and and_7 (and_7_out, not_1_out, D1_q, not_2_out);
  D_Flip_Flop D1 (.D(or_2_out), .clk(clock_1_out), .Q(D1_q), .Qn(D1_qn));  // open: preset, reset
  and and_8 (and_8_out, M1, D0_q);
  and and_9 (and_9_out, M2, D0_q);
  and and_10 (and_10_out, M2, D0_qn, M1);
  and and_11 (and_11_out, not_2_out, D1_q, D0_q, not_1_out);
  and and_12 (and_12_out, M1, D0_qn);
  and and_13 (and_13_out, not_2_out, not_1_out, D0_q);
  and and_14 (and_14_out, M2, D1_qn, D0_q);
  and and_15 (and_15_out, M2, D1_q, D0_qn);
  D_Flip_Flop D0 (.D(or_3_out), .clk(clock_1_out), .Q(D0_q), .Qn(D0_qn));  // open: preset, reset
  or or_3 (or_3_out, and_12_out, and_13_out, and_14_out, and_15_out);
  and and_16 (and_16_out, D0_qn, D1_q, not_1_out);
  and and_17 (and_17_out, D0_q, D1_q, M1);
  and and_18 (and_18_out, D1_q, M2, not_2_out);
  or or_4 (c, D1_qn, and_8_out, and_9_out, and_1_out);
  or or_5 (d, and_2_out, D1_q, and_1_out);
  or or_6 (e, D0_qn, and_6_out, and_7_out);
  or or_7 (f, and_2_out, and_7_out, and_10_out, and_11_out);
  or or_8 (g, and_16_out, and_17_out, and_18_out);
  and and_19 (L, D1_q, D0_q);

  assign b = 1'b1;
endmodule

module Modulo_servir_cafe (
  input  B,
  output LP
);

  wire and_1_out, and_2_out, and_3_out, and_4_out, clock_1_out, JK0_q, JK1_q, JK1_qn, JK2_q, JK2_qn;

  Clock clock_1 (.out(clock_1_out));
  and and_1 (and_1_out, JK0_q, JK1_q, B);
  J_K_Flip_Flop JK2 (.J(and_1_out), .K(and_2_out), .clk(clock_1_out), .Q(JK2_q), .Qn(JK2_qn));  // open: preset, reset
  and and_2 (and_2_out, B, JK1_qn);
  J_K_Flip_Flop JK1 (.J(and_3_out), .K(and_3_out), .clk(clock_1_out), .Q(JK1_q), .Qn(JK1_qn));  // open: preset, reset
  and and_3 (and_3_out, JK0_q, B);
  and and_4 (and_4_out, B, JK2_qn);
  J_K_Flip_Flop JK0 (.J(and_4_out), .K(B), .clk(clock_1_out), .Q(JK0_q));  // open: Qn, preset, reset
  and and_5 (LP, JK2_q, B);
endmodule
